// Logisim project ConverterToD8421+1.circ as structural Verilog: 1 circuit, main circuit main
module main (
  input  [3:0] D8421,
  output [3:0] D8421___1,
  output E,
  output F,
  output J,
  output H
);

  wire and_1_out, and_2_out, and_3_out, and_4_out, and_5_out, and_6_out, and_7_out, and_8_out, and_9_out,
       and_10_out, not_1_out, not_2_out, not_3_out, not_4_out;

  // Probe on D8421
  not not_1 (not_1_out, D8421[0]);
  not not_2 (not_2_out, D8421[1]);
  not not_3 (not_3_out, D8421[2]);
  not not_4 (not_4_out, D8421[3]);
  and and_1 (and_1_out, D8421[3], not_3_out, not_2_out);
  and and_2 (and_2_out, not_4_out, D8421[2], D8421[1], D8421[0]);
  and and_3 (and_3_out, not_4_out, D8421[2], not_2_out);
  and and_4 (and_4_out, not_4_out, D8421[2], not_1_out);
  and and_5 (and_5_out, not_4_out, not_3_out, D8421[1], D8421[0]);
  and and_6 (and_6_out, not_4_out, D8421[1], not_1_out);
  and and_7 (and_7_out, not_4_out, not_2_out, D8421[0]);
  and and_8 (and_8_out, not_3_out, not_2_out, D8421[0]);
  and and_9 (and_9_out, not_4_out, not_1_out);
  and and_10 (and_10_out, not_3_out, not_2_out, not_1_out);
  or or_1 (D8421___1[3], and_1_out, and_2_out);
  or or_2 (D8421___1[2], and_3_out, and_4_out, and_5_out);
  or or_3 (D8421___1[1], and_6_out, and_7_out, and_8_out);
  or or_4 (D8421___1[0], and_9_out, and_10_out);
  // Probe on D8421___1

  assign E = D8421___1[3];
  assign F = D8421___1[2];
  assign H = D8421___1[0];
  assign J = D8421___1[1];

  // Notes on the sheet:
  //   A
  //   D
  //   C
  //   B
  //   !A
  //   !D
  //   !C
  //   !B
endmodule
