// Logisim project counter_T_triggers.circ as structural Verilog: 1 circuit, main circuit main
module main (
  input  V
);

  wire clock_1_out, nand_1_out, nand_2_out, nand_3_out, nand_4_out, nand_5_out, nand_6_out, nand_7_out,
       nand_8_out;
  wire [2:0] H_q;

  // Probe on H_q
  T_Flip_Flop H (.clk(clock_1_out), .T(V), .Q(H_q[0]));  // open: Qn, preset, reset
  T_Flip_Flop I (.clk(clock_1_out), .T(nand_3_out), .Q(H_q[1]));  // open: Qn, preset, reset
  T_Flip_Flop J (.clk(clock_1_out), .T(nand_8_out), .Q(H_q[2]));  // open: Qn, preset, reset
  Clock clock_1 (.out(clock_1_out));
  nand nand_1 (nand_1_out, nand_5_out, V);
  nand nand_2 (nand_2_out, V, nand_5_out);
  nand nand_3 (nand_3_out, nand_1_out, nand_2_out);
  nand nand_4 (nand_4_out, H_q[1], H_q[1]);
  nand nand_5 (nand_5_out, H_q[0], H_q[0]);
  nand nand_6 (nand_6_out, nand_5_out, nand_4_out, V);
  nand nand_7 (nand_7_out, nand_4_out, nand_5_out, V);
  nand nand_8 (nand_8_out, nand_6_out, nand_7_out);

  // Notes on the sheet:
  //   A
  //   B
  //   C
  //   !A
  //   !B
endmodule
